// Logisim project UNRN-ED-Taller1.circ as structural Verilog: 9 circuits, main circuit SumCompleto_1bit
module SumCompleto_4bits (
  input  [3:0] A,
  input  [3:0] B,
  input  Cin,
  output [3:0] S,
  output Cout
);

  wire sumcompleto_1bit_2_cout, sumcompleto_1bit_3_cout, sumcompleto_1bit_4_cout;

  SumCompleto_1bit sumcompleto_1bit_1 (.A(B[3]), .B(A[3]), .S(S[3]), .Cin(sumcompleto_1bit_2_cout), .Cout(Cout));
  SumCompleto_1bit sumcompleto_1bit_2 (
    .A(B[2]), .B(A[2]), .S(S[2]), .Cin(sumcompleto_1bit_3_cout), .Cout(sumcompleto_1bit_2_cout));
  SumCompleto_1bit sumcompleto_1bit_3 (
    .A(B[1]), .B(A[1]), .S(S[1]), .Cin(sumcompleto_1bit_4_cout), .Cout(sumcompleto_1bit_3_cout));
  Hex_Digit_Display hex_digit_display_1 (.value(S));  // open: dp
  SumCompleto_1bit sumcompleto_1bit_4 (.A(B[0]), .B(A[0]), .S(S[0]), .Cin(Cin), .Cout(sumcompleto_1bit_4_cout));

  // Notes on the sheet:
  //   Sumador completo de 4 Bits
  //   Nro de Grupo: 8
endmodule

module SumCompleto_1bit (
  input  A,
  input  B,
  input  Cin,
  output S,
  output Cout
);

  wire and_1_out, and_2_out, xor_1_out;

  xor xor_1 (xor_1_out, A, B);
  and and_1 (and_1_out, xor_1_out, Cin);
  and and_2 (and_2_out, A, B);
  xor xor_2 (S, xor_1_out, Cin);
  or or_1 (Cout, and_1_out, and_2_out);

  // Notes on the sheet:
  //   Sumador completo de 1 Bit
  //   Nro de Grupo: 8
endmodule

module Flag_Cero (
  input  [3:0] S,
  output Z
);

  nor nor_1 (Z, S[0], S[1], S[2], S[3]);

  // Notes on the sheet:
  //   Flag - Cero (Z)
  //   Nro de Grupo: <completar>
endmodule

module Flag_Overflow (
  input  a3,
  input  b3,
  input  s3,
  output V
);

  wire and_1_out, and_2_out, not_1_out, xor_1_out;

  not not_1 (not_1_out, s3);
  and and_1 (and_1_out, b3, a3);
  and and_2 (and_2_out, not_1_out, xor_1_out);
  xor xor_1 (xor_1_out, b3, a3);
  or or_1 (V, and_2_out, and_1_out);

  // Notes on the sheet:
  //   Flag - Overflow (V)
  //   Nro de Grupo: 8
endmodule

module ComplementadorA2 (
  input  [3:0] B,
  input  Neg,
  output [3:0] B_no_neg,
  output [3:0] B_star
);

  wire not_2_out;
  wire [3:0] a_bitsandb1bit_1_s, a_bitsandb1bit_2_s, not_1_out;

  assign not_1_out = ~B;  // NOT_Gate not_1, 4 bits wide
  A_bitsAndB1bit a_bitsandb1bit_1 (.B(not_2_out), .S(a_bitsandb1bit_1_s), .A(B));
  not not_2 (not_2_out, Neg);
  SumCompleto_4bits sumcompleto_4bits_1 (.S(B_no_neg), .A(not_1_out), .B(4'b0001), .Cin(1'b0));  // open: Cout
  A_bitsAndB1bit a_bitsandb1bit_2 (.B(Neg), .S(a_bitsandb1bit_2_s), .A(B_no_neg));
  Hex_Digit_Display hex_digit_display_1 (.value(B_star));  // open: dp
  assign B_star = a_bitsandb1bit_2_s | a_bitsandb1bit_1_s;  // OR_Gate or_1, 4 bits wide

  // Notes on the sheet:
  //   Complementador a 2
  //   Nro de Grupo: 8
  //   Neg  ALU
  //   0    B
  //   1   -B
endmodule

module UnidadAritmetica (
  input  [3:0] A,
  input  [3:0] B,
  input  OP,
  output V,
  output N,
  output Z,
  output C,
  output [3:0] S
);

  Hex_Digit_Display hex_digit_display_1 (.value(S));  // open: dp

  // Notes on the sheet:
  //   Unidad Aritmetica (Suma/Resta)
  //   Nro de Grupo: <completar>
  //   OP   ALU
  //   0  A + B
  //   1  A - B
endmodule

module ALU (
  input  [3:0] A,
  input  [3:0] B,
  input  [1:0] OP,
  output V,
  output N,
  output Z,
  output C,
  output [3:0] S
);


  // Notes on the sheet:
  //   ALU (Suma/Resta/AND/OR)
  //   Nro de Grupo: <completar>
  //   OP   ALU
  //   0 0  A + B
  //   0 1  A - B
  //   1 0  A and B
  //   1 1  A or  B
endmodule

module tmp (
  input  in_1,
  input  [3:0] in_2,
  input  in_3,
  input  in_4,
  input  [3:0] in_5,
  output [3:0] out_6
);

  SumCompleto_4bits sumcompleto_4bits_1 (.S(out_6), .Cout(in_4), .A(in_2), .B(in_5), .Cin(in_3));
  Flag_Overflow flag_overflow_1 (.V(in_1), .a3(in_2[3]), .b3(in_5[3]), .s3(out_6[3]));
endmodule

module A_bitsAndB1bit (
  input  B,
  input  [3:0] A,
  output [3:0] S
);

  and and_1 (S[0], B, A[0]);
  and and_2 (S[1], B, A[1]);
  and and_3 (S[2], B, A[2]);
  and and_4 (S[3], B, A[3]);
endmodule
