// Logisim project t1_v2.circ as structural Verilog: 8 circuits, main circuit SumCompleto_1bit
module SumCompleto_4bits (
  input  [3:0] A,
  input  [3:0] B,
  input  Cin,
  output [3:0] S,
  output Cout
);

  wire sumcompleto_1bit_2_cout, sumcompleto_1bit_3_cout, sumcompleto_1bit_4_cout;

  SumCompleto_1bit sumcompleto_1bit_1 (.A(B[3]), .B(A[3]), .S(S[3]), .Cin(sumcompleto_1bit_2_cout), .Cout(Cout));
  SumCompleto_1bit sumcompleto_1bit_2 (
    .A(B[2]), .B(A[2]), .S(S[2]), .Cin(sumcompleto_1bit_3_cout), .Cout(sumcompleto_1bit_2_cout));
  SumCompleto_1bit sumcompleto_1bit_3 (
    .A(B[1]), .B(A[1]), .S(S[1]), .Cin(sumcompleto_1bit_4_cout), .Cout(sumcompleto_1bit_3_cout));
  Hex_Digit_Display hex_digit_display_1 (.value(S));  // open: dp
  SumCompleto_1bit sumcompleto_1bit_4 (.A(B[0]), .B(A[0]), .S(S[0]), .Cin(Cin), .Cout(sumcompleto_1bit_4_cout));

  // Notes on the sheet:
  //   Sumador completo de 4 Bits
  //   Nro de Grupo: 8
endmodule

module SumCompleto_1bit (
  input  A,
  input  B,
  input  Cin,
  output S,
  output Cout
);

  wire and_1_out, and_2_out, xor_1_out;

  xor xor_1 (xor_1_out, A, B);
  and and_1 (and_1_out, xor_1_out, Cin);
  and and_2 (and_2_out, A, B);
  xor xor_2 (S, xor_1_out, Cin);
  or or_1 (Cout, and_1_out, and_2_out);

  // Notes on the sheet:
  //   Sumador completo de 1 Bit
  //   Nro de Grupo: 8
endmodule

module Flag_Cero (
  input  [3:0] S,
  output Z
);

  nor nor_1 (Z, S[0], S[1], S[2], S[3]);

  // Notes on the sheet:
  //   Flag - Cero (Z)
  //   Nro de Grupo: <completar>
endmodule

module Flag_Overflow (
  input  a3,
  input  b3,
  input  s3,
  output V
);

  wire and_1_out, and_2_out, not_1_out, xor_1_out;

  not not_1 (not_1_out, s3);
  and and_1 (and_1_out, b3, a3);
  and and_2 (and_2_out, not_1_out, xor_1_out);
  xor xor_1 (xor_1_out, b3, a3);
  or or_1 (V, and_2_out, and_1_out);

  // Notes on the sheet:
  //   Flag - Overflow (V)
  //   Nro de Grupo: 8
endmodule

module ComplementadorA2 (
  input  [3:0] B,
  input  Neg,
  output Cout,
  output [3:0] B_star
);

  wire [3:0] not_1_out, sumcompleto_4bits_1_s;

  assign not_1_out = ~B;  // NOT_Gate not_1, 4 bits wide
  SumCompleto_4bits sumcompleto_4bits_1 (
    .S(sumcompleto_4bits_1_s), .Cout(Cout), .A(4'b0001), .B(not_1_out), .Cin(1'b0));
  Hex_Digit_Display hex_digit_display_1 (.value(B_star));  // open: dp
  Multiplexer #(.width(4)) multiplexer_1 (.in0(B), .in1(sumcompleto_4bits_1_s), .out(B_star), .sel(Neg), .en(1'b1));

  // Notes on the sheet:
  //   Complementador a 2
  //   Nro de Grupo: 8
  //   Neg  ALU
  //   0    B
  //   1   -B
endmodule

module UnidadAritmetica (
  input  [3:0] A,
  input  [3:0] B,
  input  Cin,
  input  OP,
  output Cout,
  output V,
  output N,
  output Z,
  output C,
  output [3:0] S,
  output [3:0] S_2
);

  wire not_1_out, not_2_out, sumcompleto_4bits_1_cout;
  wire [3:0] complementadora2_1_b_star;

  SumCompleto_4bits sumcompleto_4bits_1 (
    .S(S), .Cout(sumcompleto_4bits_1_cout), .A(A), .B(complementadora2_1_b_star), .Cin(Cin));
  Flag_Overflow flag_overflow_1 (.V(V), .a3(A[3]), .b3(complementadora2_1_b_star[3]), .s3(S[3]));
  Hex_Digit_Display hex_digit_display_1 (.value(A));  // open: dp
  ComplementadorA2 complementadora2_1 (.B_star(complementadora2_1_b_star), .B(B), .Cout(Cout), .Neg(OP));
  Hex_Digit_Display hex_digit_display_2 (.value(B));  // open: dp
  Flag_Cero flag_cero_1 (.Z(Z), .S(S));
  not not_1 (not_1_out, sumcompleto_4bits_1_cout);
  not not_2 (not_2_out, OP);
  and and_1 (N, OP, not_1_out);
  and and_2 (C, sumcompleto_4bits_1_cout, not_2_out);
  Hex_Digit_Display hex_digit_display_3 (.value(S));  // open: dp
  ComplementadorA2 complementadora2_2 (.B_star(S_2), .B(S), .Neg(1'b1));  // open: Cout
  Hex_Digit_Display hex_digit_display_4 (.value(S_2));  // open: dp

  // Notes on the sheet:
  //   Unidad Aritmetica (Suma/Resta)
  //   Nro de Grupo: 8
  //   OP   ALU
  //   0  A + B
  //   1  A - B
endmodule

module ALU (
  input  [3:0] A,
  input  [3:0] B,
  input  [1:0] OP,
  output V,
  output N,
  output Z,
  output C,
  output [3:0] S
);

  wire [3:0] and_1_out, or_1_out, unidadaritmetica_1_s;

  Hex_Digit_Display hex_digit_display_1 (.value(A));  // open: dp
  UnidadAritmetica unidadaritmetica_1 (
    .OP(OP[0]), .V(V), .N(N), .Z(Z), .C(C), .S(unidadaritmetica_1_s), .A(A), .B(B), .Cin(1'b0));  // open: Cout, S_2
  Hex_Digit_Display hex_digit_display_2 (.value(B));  // open: dp
  assign and_1_out = B & A;  // AND_Gate and_1, 4 bits wide
  assign or_1_out = B | A;  // OR_Gate or_1, 4 bits wide
  Multiplexer #(.select(2), .width(4)) multiplexer_1 (
    .in0(unidadaritmetica_1_s), .in1(unidadaritmetica_1_s), .in2(and_1_out), .in3(or_1_out), .out(S),
    .sel(OP), .en(1'b1));
  Hex_Digit_Display hex_digit_display_3 (.value(S));  // open: dp

  // Notes on the sheet:
  //   ALU (Suma/Resta/AND/OR)
  //   Nro de Grupo: 8
  //   OP   ALU
  //   0 0  A + B
  //   0 1  A - B
  //   1 0  A and B
  //   1 1  A or  B
endmodule

module tmp (
  input  in_1,
  input  [3:0] in_2,
  input  in_3,
  input  in_4,
  input  [3:0] in_5,
  output [3:0] out_6
);

  SumCompleto_4bits sumcompleto_4bits_1 (.S(out_6), .Cout(in_4), .A(in_2), .B(in_5), .Cin(in_3));
  Flag_Overflow flag_overflow_1 (.V(in_1), .a3(in_2[3]), .b3(in_5[3]), .s3(out_6[3]));
endmodule
